// Logisim project Lab3MS1.circ as structural Verilog
module ALU_control (
  input  i30,
  input  i14,
  input  i13,
  input  i12,
  input  i6,
  input  i5,
  input  i4,
  output aluc3,
  output aluc2,
  output aluc1,
  output aluc0,
  output alusrc
);

  wire and_1_out, not_1_out, not_2_out, not_3_out, not_4_out, not_5_out;

  not not_1 (not_1_out, i14);
  not not_2 (not_2_out, i13);
  not not_3 (not_3_out, i12);
  not not_4 (not_4_out, i5);
  not not_5 (not_5_out, i4);
  or or_1 (aluc1, not_2_out, not_5_out);
  and and_1 (and_1_out, i13, not_3_out);
  or or_2 (alusrc, not_4_out, not_5_out);
  or or_3 (aluc0, not_1_out, and_1_out);

  assign aluc2 = 1'b0;
  assign aluc3 = 1'b0;
endmodule
